# Fritzing sketch touchy (saved by Fritzing 0.9.2b)
breadboards: 1

parts:
  U1 = EDISON
  S1 = Pushbutton [package="[THT]"]
  Q1 = NPN-Transistor [package="TO92 [THT]"]
  LED1 = LED - 5mm [color="Red (633nm)" package="5 mm [THT]"]
  R1 = Resistor [tolerance=±5% resistance=220 package=THT]

nets:
  N1: U1.GP134, S1.Pin_1, S1.Pin_2, Q1.C
  N2: U1.GP49, Q1.B
  N3: U1.V_V1P80, R1.Pin_0
  N4: U1.GP48, S1.Pin_3, S1.Pin_4
  N5: Q1.E, LED1.cathode
  N6: LED1.anode, R1.Pin_1
